# Fritzing sketch lobstar-0.2 (saved by Fritzing 0.8.3b)
circuit board: 5.93217cm x 2.52822cm
breadboards: 1

parts:
  J1 = male pin header, 6 pins [form="♂ (male)"]
  J3 = male pin header, 14 pins [form="♂ (male)"]
  J2 = male pin header, 14 pins [form="♂ (male)"]
  C1 = Ceramic Capacitor [capacitance=0.1nF package="100 mil [THT, multilayer]"]
  Y1 = Resonator [frequency="16 Mhz" package=THT]
  R1 = Resistor [tolerance=±5% resistance=1k package=THT]
  U1 = atmega168 [package=dip]

nets:
  N1: J1.pin1, C1.0
  N2: J1.pin2, J2.pin3, U1.D1_(TX)
  N3: J1.pin3, J2.pin2, U1.D0_(RX)
  N4: J1.pin4, J3.pin9, J2.pin7, R1.Pin_0, U1.VCC, U1.AVCC
  GND: J1.pin6, J3.pin7, J2.pin8, Y1.GND, U1.GND
  N5: J3.pin1, U1.A5
  N6: J3.pin2, U1.A4
  N7: J3.pin3, U1.A3
  N8: J3.pin4, U1.A2
  N9: J3.pin5, U1.A1
  N10: J3.pin6, U1.A0
  N11: J3.pin8, U1.AREF
  N12: J3.pin10, U1.D13
  N13: J3.pin11, U1.D12
  N14: J3.pin12, U1.D11_(PWM)
  N15: J3.pin13, U1.D10_(PWM)
  N16: J3.pin14, U1.D9_(PWM)
  N17: J2.pin1, C1.1, R1.Pin_1, U1.RESET
  N18: J2.pin4, U1.D2
  N19: J2.pin5, U1.D3_(PWM)
  N20: J2.pin6, U1.D4
  N21: J2.pin9, Y1.0, U1.XLAT1
  N22: J2.pin10, Y1.pin_1, U1.XLAT2
  N23: J2.pin11, U1.D5_(PWM)
  N24: J2.pin12, U1.D6_(PWM)
  N25: J2.pin13, U1.D7
  N26: J2.pin14, U1.D8

notes:
  boarduinette v 0.1
